# Fritzing sketch ReceiverCircuit (saved by Fritzing 0.9.2b)
breadboards: 1

parts:
  Part1 = Arduino Micro (Rev3)
  Part2 = Bluetooth HC-05 Macho
  R2 = Resistor [tolerance=±5% resistance=220 package="1206 [SMD]"]
  LED1 = LED - 3mm [color="Red (633nm)" package="3 mm [THT]"]
  LED2 = LED - 5mm [color="Yellow (595nm)" package="5 mm [THT]"]
  R3 = Resistor [tolerance=±5% resistance=220 package="1206 [SMD]"]
  J1 = Basic Servo
  Not_really_tempereature_but_SS41_HallEffect = LM35 Temperature Sensor [package="TO92 [THT]"]
  Relay = Screw terminal - 2 pins [package=THT]

nets:
  N1: Part1.D1/TX, Part2.RXD
  N2: Part1.D0/RX, Part2.TXD
  N3: Part1.D2/SDA, Not_really_tempereature_but_SS41_HallEffect.GND
  N4: Part1.D3/SCL, Part1.D9_PWM/A9, J1.pulse
  N5: Part1.D4_PWM/A6, R2.Pin_0
  N6: Part1.D5_PWM, Relay.pin1
  N7: Part1.D6_PWM/A7, R3.Pin_0
  GND: Part1.GND, Part2.GND, LED1.cathode, LED2.cathode, J1.gnd, Not_really_tempereature_but_SS41_HallEffect.Vout, Relay.pin2
  VCC: Part1.5V, Part2.VCC, J1.vcc, Not_really_tempereature_but_SS41_HallEffect.+Vs
  N8: R2.Pin_1, LED1.anode
  N9: LED2.anode, R3.Pin_1

custom parts:
  LM35 Temperature Sensor: A LM35 temperature sensor with a temperature range from -55°C to 150°C.
